// Logisim project ALU32.circ as structural Verilog: 6 circuits, main circuit ALU32
module ALU32 (
  input  [4:0] Sa,
  input  [31:0] A,
  input  [31:0] B,
  input  [3:0] Op,
  output V,
  output [31:0] C
);

  wire not_1_out, y, z;
  wire [31:0] _0_1, _2_3, _4, _6_7, _8, _09, _10, _12_11, _13, _14, _15, LeftShift32_3_c, not_2_out;

  not not_1 (not_1_out, 1'b1);
  LeftShift32 LeftShift32 (.Cin(not_1_out), .B(B), .Sa(Sa), .C(_0_1));
  assign not_2_out = ~B;  // NOT_Gate not_2, 32 bits wide
  Add32 Add32 (.A(A), .B(B), .Cin(not_1_out), .C(_2_3), .V(z));
  LeftShift32 LeftShift32_2 (
    .Cin(not_1_out),
    .B({B[0], B[1], B[2], B[3], B[4], B[5], B[6], B[7], B[8], B[9], B[10], B[11], B[12], B[13], B[14], B[15], B[16], B[17], B[18], B[19], B[20], B[21], B[22], B[23], B[24], B[25], B[26], B[27], B[28], B[29], B[30], B[31]}),
    .Sa(Sa),
    .C({_4[0], _4[1], _4[2], _4[3], _4[4], _4[5], _4[6], _4[7], _4[8], _4[9], _4[10], _4[11], _4[12], _4[13], _4[14], _4[15], _4[16], _4[17], _4[18], _4[19], _4[20], _4[21], _4[22], _4[23], _4[24], _4[25], _4[26], _4[27], _4[28], _4[29], _4[30], _4[31]}));
  Add32 Add32_2 (.A(A), .B(not_2_out), .Cin(1'b1), .C(_6_7), .V(y));
  assign _8 = A & B;  // AND_Gate AND, 32 bits wide
  assign _10 = A | B;  // OR_Gate OR, 32 bits wide
  assign _12_11 = A ^ B;  // XOR_Gate XOR, 32 bits wide
  assign _14 = ~(A | B);  // NOR_Gate NOR, 32 bits wide
  assign _09 = ~_12_11;  // NOT_Gate not_3, 32 bits wide
  assign _13 = _12_11 & A;  // AND_Gate and_2, 32 bits wide
  LeftShift32 LeftShift32_3 (
    .Cin(B[31]),
    .B({B[0], B[1], B[2], B[3], B[4], B[5], B[6], B[7], B[8], B[9], B[10], B[11], B[12], B[13], B[14], B[15], B[16], B[17], B[18], B[19], B[20], B[21], B[22], B[23], B[24], B[25], B[26], B[27], B[28], B[29], B[30], B[31]}),
    .Sa(Sa), .C(LeftShift32_3_c));
  assign _15 = ~_13;  // NOT_Gate not_4, 32 bits wide
  Multiplexer #(.select(4)) multiplexer_1 (
    .in0(not_1_out), .in1(not_1_out), .in2(z), .in3(z), .in4(not_1_out), .in5(not_1_out), .in6(y), .in7(y),
    .in8(not_1_out), .in9(not_1_out), .in10(not_1_out), .in11(not_1_out), .in12(not_1_out), .in13(not_1_out),
    .in14(not_1_out), .in15(not_1_out), .out(V), .sel(Op));  // open: en
  Multiplexer #(.select(4), .width(32)) multiplexer_2 (
    .in0(_0_1), .in1(_0_1), .in2(_2_3), .in3(_2_3), .in4(_4),
    .in5({LeftShift32_3_c[0], LeftShift32_3_c[1], LeftShift32_3_c[2], LeftShift32_3_c[3], LeftShift32_3_c[4], LeftShift32_3_c[5], LeftShift32_3_c[6], LeftShift32_3_c[7], LeftShift32_3_c[8], LeftShift32_3_c[9], LeftShift32_3_c[10], LeftShift32_3_c[11], LeftShift32_3_c[12], LeftShift32_3_c[13], LeftShift32_3_c[14], LeftShift32_3_c[15], LeftShift32_3_c[16], LeftShift32_3_c[17], LeftShift32_3_c[18], LeftShift32_3_c[19], LeftShift32_3_c[20], LeftShift32_3_c[21], LeftShift32_3_c[22], LeftShift32_3_c[23], LeftShift32_3_c[24], LeftShift32_3_c[25], LeftShift32_3_c[26], LeftShift32_3_c[27], LeftShift32_3_c[28], LeftShift32_3_c[29], LeftShift32_3_c[30], LeftShift32_3_c[31]}),
    .in6(_6_7), .in7(_6_7), .in8(_8), .in9(_09), .in10(_10), .in11(_12_11), .in12(_12_11), .in13(_13),
    .in14(_14), .in15(_15), .out(C), .sel(Op));  // open: en
endmodule

module Add32 (
  input  [31:0] A,
  input  [31:0] B,
  input  Cin,
  output [31:0] C,
  output V
);

  wire _16BitAdder_v;

  _16BitAdder _16BitAdder (.A(A[15:0]), .B(B[15:0]), .Cin(Cin), .C(C[15:0]), .V(_16BitAdder_v));
  _16BitAdder _16BitAdder_2 (.A(A[31:16]), .B(B[31:16]), .Cin(_16BitAdder_v), .C(C[31:16]), .V(V));
endmodule

module _1bitadder (
  input  A,
  input  B,
  input  Cin,
  output C,
  output V
);

  wire and_1_out, and_2_out, and_3_out, and_4_out, and_5_out, and_6_out, and_7_out, not_1_out, not_2_out,
       not_3_out, not_4_out, not_5_out, not_6_out;

  not not_1 (not_1_out, A);
  not not_2 (not_2_out, B);
  not not_3 (not_3_out, A);
  not not_4 (not_4_out, Cin);
  not not_5 (not_5_out, B);
  not not_6 (not_6_out, Cin);
  and and_1 (and_1_out, not_1_out, not_2_out, Cin);
  and and_2 (and_2_out, not_3_out, B, not_4_out);
  and and_3 (and_3_out, A, not_5_out, not_6_out);
  and and_4 (and_4_out, A, B, Cin);
  and and_5 (and_5_out, B, Cin);
  or or_1 (V, and_5_out, and_6_out, and_7_out);
  and and_6 (and_6_out, A, Cin);
  and and_7 (and_7_out, A, B);
  or or_2 (C, and_1_out, and_2_out, and_3_out, and_4_out);
endmodule

module _4bitadder (
  input  [3:0] A,
  input  [3:0] B,
  input  Cin,
  output [3:0] C,
  output V
);

  wire _1BitAdder_2_v, _1BitAdder_3_v, _1BitAdder_v;

  _1bitadder _1BitAdder (.A(A[0]), .B(B[0]), .Cin(Cin), .C(C[0]), .V(_1BitAdder_v));
  _1bitadder _1BitAdder_2 (.A(A[1]), .B(B[1]), .Cin(_1BitAdder_v), .C(C[1]), .V(_1BitAdder_2_v));
  _1bitadder _1BitAdder_3 (.A(A[2]), .B(B[2]), .Cin(_1BitAdder_2_v), .C(C[2]), .V(_1BitAdder_3_v));
  _1bitadder _1BitAdder_4 (.A(A[3]), .B(B[3]), .Cin(_1BitAdder_3_v), .C(C[3]), .V(V));
endmodule

module _16BitAdder (
  input  [15:0] A,
  input  [15:0] B,
  input  Cin,
  output [15:0] C,
  output V
);

  wire _4BitAdder_2_v, _4BitAdder_3_v, _4BitAdder_v;

  _4bitadder _4BitAdder (.A(A[3:0]), .B(B[3:0]), .Cin(Cin), .C(C[3:0]), .V(_4BitAdder_v));
  _4bitadder _4BitAdder_2 (.A(A[7:4]), .B(B[7:4]), .Cin(_4BitAdder_v), .C(C[7:4]), .V(_4BitAdder_2_v));
  _4bitadder _4BitAdder_3 (.A(A[11:8]), .B(B[11:8]), .Cin(_4BitAdder_2_v), .C(C[11:8]), .V(_4BitAdder_3_v));
  _4bitadder _4BitAdder_4 (.A(A[15:12]), .B(B[15:12]), .Cin(_4BitAdder_3_v), .C(C[15:12]), .V(V));
endmodule

module LeftShift32 (
  input  Cin,
  input  [31:0] B,
  input  [4:0] Sa,
  output [31:0] C
);

  wire [31:0] multiplexer_1_out, multiplexer_2_out, multiplexer_3_out, multiplexer_4_out;

  Multiplexer #(.width(32)) multiplexer_1 (
    .in0({B[31:15], {15{B[15]}}}), .in1({B[31:15], {15{B[15]}}}), .out(multiplexer_1_out), .sel(Sa[4]));  // open: en
  Multiplexer #(.width(32)) multiplexer_2 (
    .in0(multiplexer_1_out), .in1({multiplexer_1_out[23:0], {8{B[15]}}}), .out(multiplexer_2_out), .sel(Sa[3]));  // open: en
  Multiplexer #(.width(32)) multiplexer_3 (
    .in0(multiplexer_2_out), .in1({multiplexer_2_out[27:0], {4{B[15]}}}), .out(multiplexer_3_out), .sel(Sa[2]));  // open: en
  Multiplexer #(.width(32)) multiplexer_4 (
    .in0(multiplexer_3_out), .in1({multiplexer_3_out[29:0], {2{B[15]}}}), .out(multiplexer_4_out), .sel(Sa[1]));  // open: en
  Multiplexer #(.width(32)) multiplexer_5 (
    .in0(multiplexer_4_out), .in1({multiplexer_4_out[30:0], B[15]}), .out(C), .sel(Sa[0]));  // open: en

  assign B[14:0] = {15{B[15]}};
  assign Cin = B[15];
endmodule
