// Logisim project ROMHarvardDesign.circ as structural Verilog: 6 circuits, main circuit main
module main (
  input  [31:0] in_1
);

  wire ALUSrc, clock_1_out, RegDst, registerfile_1_p1, registerfile_1_p7, RegWE;
  wire [3:0] ALUOp;
  wire [4:0] multiplexer_1_out;
  wire [31:0] mips_alu_1_p2, mipsprogramrom_1_p2, registerfile_1_p8, Sign_Extender_b;

  Clock clock_1 (.out(clock_1_out));
  // MIPSProgramROM mipsprogramrom_1: pin names not known; wires that end beside it: in_1, mipsprogramrom_1_p2
  control Control (
    .Instruction_26_31(mipsprogramrom_1_p2[31:26]), .Instruction_0_5(mipsprogramrom_1_p2[5:0]),
    .RegDst(RegDst), .ALUSrc(ALUSrc), .RegWrite(RegWE), .Op(ALUOp));
  Multiplexer #(.width(5)) multiplexer_1 (
    .in0(mipsprogramrom_1_p2[20:16]), .in1(mipsprogramrom_1_p2[15:11]), .out(multiplexer_1_out), .sel(RegDst));  // open: en
  sign_extender Sign_Extender (.Instruction(mipsprogramrom_1_p2[15:0]), .B(Sign_Extender_b));
  // RegisterFile registerfile_1: pin names not known; wires that end beside it: registerfile_1_p1, clock_1_out, RegWE, multiplexer_1_out, mipsprogramrom_1_p2[25:21], mipsprogramrom_1_p2[20:16], registerfile_1_p7, registerfile_1_p8
  // Mips_ALU mips_alu_1: pin names not known; wires that end beside it: registerfile_1_p7, mips_alu_1_p2, ALUOp, mipsprogramrom_1_p2[10:6], registerfile_1_p1
  Multiplexer #(.width(32)) multiplexer_2 (
    .in0(registerfile_1_p8), .in1(Sign_Extender_b), .out(mips_alu_1_p2), .sel(ALUSrc));  // open: en
endmodule

module sign_extender (
  input  [15:0] Instruction,
  output [31:0] B
);


  assign B = {{17{Instruction[15]}}, Instruction[14:0]};
endmodule

module control (
  input  [5:0] Instruction_26_31,
  input  [5:0] Instruction_0_5,
  output RegDst,
  output ALUSrc,
  output RegWrite,
  output [3:0] Op
);

  wire [3:0] op_1_op, special_op_1_op;

  Special_Op special_op_1 (.Instruction(Instruction_0_5), .Op(special_op_1_op));
  Op op_1 (.Instruction(Instruction_26_31), .Op(op_1_op));
  or or_1 (ALUSrc, Instruction_26_31[0], Instruction_26_31[1], Instruction_26_31[2], Instruction_26_31[3], Instruction_26_31[4], Instruction_26_31[5]);
  not not_1 (RegDst, ALUSrc);
  Multiplexer #(.width(4)) multiplexer_1 (.in0(special_op_1_op), .in1(op_1_op), .out(Op), .sel(ALUSrc));  // open: en

  assign RegWrite = 1'b1;
endmodule

module PC (
  input  [31:0] in_1,
  output [31:0] out_2
);

  // Incrementer incrementer_1: pin names not known; wires that end beside it: in_1[9:2], out_2[9:2]
endmodule

module Op (
  input  [5:0] Instruction,
  output [3:0] Op
);

  wire not_1_out, not_2_out, not_3_out, not_4_out;

  not not_1 (not_1_out, Instruction[3]);
  not not_2 (not_2_out, Instruction[3]);
  not not_3 (not_3_out, Instruction[2]);
  not not_4 (not_4_out, Instruction[1]);
  not not_5 (Op[0], Instruction[2]);
  or or_1 (Op[3], not_1_out, Instruction[0], Instruction[1]);
  or or_2 (Op[2], not_2_out, Instruction[1]);
  or or_3 (Op[1], not_3_out, not_4_out);
endmodule

module Special_Op (
  input  [5:0] Instruction,
  output [3:0] Op
);

  wire and_1_out, and_2_out, and_3_out, and_4_out, and_5_out, and_6_out, and_7_out, not_1_out, not_2_out,
       not_3_out, not_4_out;

  and and_1 (and_1_out, Instruction[5], Instruction[2]);
  not not_1 (not_1_out, Instruction[3]);
  not not_2 (not_2_out, Instruction[2]);
  not not_3 (not_3_out, Instruction[0]);
  not not_4 (not_4_out, Instruction[5]);
  or or_1 (Op[3], Instruction[3], and_1_out);
  and and_2 (and_2_out, not_1_out, Instruction[1], Instruction[0]);
  and and_3 (and_3_out, Instruction[2], Instruction[1]);
  and and_4 (and_4_out, Instruction[5], Instruction[1]);
  and and_5 (and_5_out, not_2_out, Instruction[1], not_3_out);
  and and_6 (and_6_out, Instruction[5], Instruction[0]);
  and and_7 (and_7_out, not_4_out, Instruction[0]);
  or or_2 (Op[2], and_2_out, and_3_out, and_4_out);
  or or_3 (Op[1], and_5_out, and_6_out);
  or or_4 (Op[0], and_7_out, Instruction[3]);
endmodule
